# Fritzing sketch piezo (saved by Fritzing 0.9.4)

parts:
  Bauteil1 = Arduino Uno (Rev3)
  R1 = Resistor [tolerance=±5% resistance=220 package=THT]
  J1 = Piezo Speaker
  R2 = Rotary Potentiometer (Small) [maximum_resistance=100kΩ package=THT]

nets:
  N1: Bauteil1.A0, R2.wiper
  N2: Bauteil1.D13/SCK, J1.pin2
  N3: Bauteil1.GND, R1.Pin_0, R2.leg1
  N4: Bauteil1.5V, R2.leg2
  N5: R1.Pin_1, J1.pin1
